// Logisim project 8_bit_basic_cpu.circ as structural Verilog: 3 circuits, main circuit main
module main (
  output [7:0] out_1,
  output [4:0] out_2,
  output [4:0] out_3,
  output [7:0] out_4,
  output E,
  output [7:0] out_6,
  output [7:0] out_7
);

  wire AC_LD, ADD_BGN, ADD_END, AND_BGN, AND_END, AR_LD, BUN_BGN, CLK, decoder_2_out0, decoder_2_out1,
       decoder_2_out2, decoder_2_out3, decoder_2_out4, DR_LD, IR_LD, LDA_BGN, LDA_END, MM_READ, MM_WRITE,
       or_1_out, or_6_out, SEL_AC, SEL_AR, SEL_DR, SEL_IR, SEL_MM, SEL_PC, T0, T2, T3, T4;
  wire [2:0] SELECTION;
  wire [4:0] bit_extender_1_out, bit_extender_2_out;
  wire [7:0] AC_DIN, adder_1_out, and_1_out, bit_extender_3_out, bit_extender_4_out, bit_extender_5_out,
       ram_1_data;

  Bit_Extender #(.out_width(5)) bit_extender_1 (.in(out_1), .out(bit_extender_1_out));
  Bit_Extender #(.out_width(5)) bit_extender_2 (.in(out_1), .out(bit_extender_2_out));
  RAM #(.addrWidth(5), .bus("separate")) ram_1 (
    .addr(out_2), .din(out_1), .data(ram_1_data), .str(MM_WRITE), .clk(CLK), .ld(MM_READ));  // open: sel, clr
  Register #(.width(5)) AR (.D(bit_extender_1_out), .en(AR_LD), .Q(out_2), .clk(CLK));  // open: clr
  Counter #(.width(5), .max('h1f)) PC (
    .load(BUN_BGN), .D(bit_extender_2_out), .count(IR_LD), .Q(out_3), .clk(CLK));  // open: carry, clr
  Register DR (.D(out_1), .en(DR_LD), .Q(out_4), .clk(CLK));  // open: clr
  Register AC (.D(AC_DIN), .en(AC_LD), .Q(out_6), .clk(CLK));  // open: clr
  Register IR (.D(out_1), .en(IR_LD), .Q(out_7), .clk(CLK));  // open: clr
  Hex_Digit_Display hex_digit_display_1 (.value(out_6[7:4]));  // open: dp
  Hex_Digit_Display hex_digit_display_2 (.value(out_6[3:0]));  // open: dp
  assign out_1 = SEL_MM ? ram_1_data : 8'bz;  // Controlled_Buffer controlled_buffer_1
  assign bit_extender_3_out = {{3{1'b0}}, out_2};  // Bit_Extender bit_extender_3
  assign out_1 = SEL_AR ? bit_extender_3_out : 8'bz;  // Controlled_Buffer controlled_buffer_2
  assign out_1 = SEL_PC ? bit_extender_4_out : 8'bz;  // Controlled_Buffer controlled_buffer_3
  assign bit_extender_4_out = {{3{1'b0}}, out_3};  // Bit_Extender bit_extender_4
  assign out_1 = SEL_DR ? out_4 : 8'bz;  // Controlled_Buffer controlled_buffer_4
  assign out_1 = SEL_AC ? out_6 : 8'bz;  // Controlled_Buffer controlled_buffer_5
  assign out_1 = SEL_IR ? bit_extender_5_out : 8'bz;  // Controlled_Buffer controlled_buffer_6
  assign bit_extender_5_out = {{3{1'b0}}, out_7[4:0]};  // Bit_Extender bit_extender_5
  Clock clock_1 (.out(CLK));
  Decoder #(.select(3), .disabled(0), .enable("false")) decoder_1 (
    .out1(SEL_AR), .out2(SEL_PC), .out3(SEL_DR), .out4(SEL_AC), .out5(SEL_IR), .out7(SEL_MM), .sel(SELECTION));  // open: out0, out6
  SC_support_circuit sc_support_circuit_1 (.CLK(CLK), .CLR(or_1_out), .T0(T0), .T1(IR_LD), .T2(T2), .T3(T3), .T4(T4));
  or or_1 (or_1_out, AND_END, ADD_END, LDA_END, MM_WRITE, BUN_BGN);
  or or_2 (AR_LD, T0, T2);
  or or_3 (DR_LD, AND_BGN, ADD_BGN, LDA_BGN);
  or or_4 (AC_LD, AND_END, ADD_END, LDA_END);
  or or_5 (MM_READ, AND_BGN, ADD_BGN, LDA_BGN, IR_LD);
  assign and_1_out = out_4 & out_6;  // AND_Gate and_1, 8 bits wide
  Adder adder_1 (.a(out_6), .b(out_4), .out(adder_1_out), .cout(E));  // open: cin
  Multiplexer #(.select(2), .width(8), .enable("false")) multiplexer_1 (
    .in0(out_4), .in1(and_1_out), .in2(adder_1_out), .out(AC_DIN), .sel({ADD_END, AND_END}));  // open: in3
  Decoder #(.select(3), .enable("false")) decoder_2 (
    .out0(decoder_2_out0), .out1(decoder_2_out1), .out2(decoder_2_out2), .out3(decoder_2_out3),
    .out4(decoder_2_out4), .sel(out_7[7:5]));  // open: out5, out6, out7
  and D0T3 (AND_BGN, decoder_2_out0, T3);
  and D1T3 (ADD_BGN, decoder_2_out1, T3);
  and D2T3 (LDA_BGN, decoder_2_out2, T3);
  and D3T3 (MM_WRITE, decoder_2_out3, T3);
  and D4T3 (BUN_BGN, decoder_2_out4, T3);
  and D0T4 (AND_END, decoder_2_out0, T4);
  and D1T4 (ADD_END, decoder_2_out1, T4);
  and D2T4 (LDA_END, decoder_2_out2, T4);
  or or_6 (or_6_out, AND_BGN, ADD_BGN, LDA_BGN, IR_LD);
  encoder encoder_1 (
    .D7(or_6_out), .D6(1'b0), .D5(T2), .D4(MM_WRITE), .D3(LDA_END), .D2(T0), .D1(BUN_BGN), .out_8(SELECTION));

  // Other names for the same wires on the sheet: AC_DOUT[7:0] = out_6; AR_DOUT[4:0] = out_2; BUS[7:0] = out_1;
  //   DR_DOUT[7:0] = out_4; IR_DOUT[7:0] = out_7; OPCODE[2:0] = out_7[7:5]; PC_DOUT[4:0] = out_3; PC_LD = BUN_BGN;
  //   STA_BGN = MM_WRITE; PC_INR = IR_LD; T1 = IR_LD

  // Notes on the sheet:
  //   AddLoop Program Test
  //   Timing Control
  //   Currently on bus:
  //   Load control
  //   Calculation
  //   Decode
  //   Bus Selection
  //   7
  //   1
endmodule

module SC_support_circuit (
  input  CLK,
  input  CLR,
  output T0,
  output T1,
  output T2,
  output T3,
  output T4
);

  wire d_ff_1_q, decoder_1_out5, decoder_1_out6, decoder_1_out7, or_1_out;
  wire [2:0] counter_1_q;

  Counter #(.width(3), .max('h7)) counter_1 (
    .count(1'b1), .Q(counter_1_q), .clk(CLK), .clr(or_1_out));  // open: load, D, carry
  Decoder #(.select(3), .enable("false")) decoder_1 (
    .out0(T0), .out1(T1), .out2(T2), .out3(T3), .out4(T4), .out5(decoder_1_out5), .out6(decoder_1_out6),
    .out7(decoder_1_out7), .sel(counter_1_q));
  or or_1 (or_1_out, decoder_1_out7, decoder_1_out6, decoder_1_out5, d_ff_1_q);
  D_Flip_Flop d_ff_1 (.clk(CLK), .D(CLR), .Q(d_ff_1_q));  // open: Qn, preset, en, reset
endmodule

module encoder (
  input  D7,
  input  D6,
  input  D5,
  input  D4,
  input  D3,
  input  D2,
  input  D1,
  output [2:0] out_8
);

  or _4_5_6_7 (out_8[2], D7, D6, D5, D4);
  or _2_3_6_7 (out_8[1], D7, D6, D3, D2);
  or _1_3_5_7 (out_8[0], D7, D5, D3, D1);
endmodule
